# Fritzing sketch LEDAndButton (saved by Fritzing 0.9.3b)
breadboards: 1

parts:
  Arduino_UNO = Arduino Uno (Rev3) - ICSP
  R2 = Resistor [tolerance=±5% resistance=10k package="0402 [SMD]"]
  R1 = Resistor [tolerance=±5% resistance=470 package="0402 [SMD]"]
  LED1 = LED - 5mm [color="Red (633nm)" package="5 mm [THT]"]
  S1 = Pushbutton [package="[THT]"]

nets:
  N1: Arduino_UNO.5V, S1.Pin_1, S1.Pin_2
  N2: Arduino_UNO.D8, LED1.anode
  N3: Arduino_UNO.D2, R2.Pin_0, S1.Pin_3, S1.Pin_4
  N4: Arduino_UNO.GND, R2.Pin_1, R1.Pin_1
  N5: R1.Pin_0, LED1.cathode
