# Fritzing sketch LED Project (saved by Fritzing 0.9.3b)

parts:
  Part1 = Arduino Uno (Rev3)
  8_digit_7_segment_LED_Module_with_Max1 = 8 digit 7 segment LED Module with MAX7219 [package=THT]

nets:
  N1: Part1.D10_PWM/SS, 8_digit_7_segment_LED_Module_with_Max1.CS
  N2: Part1.D11_PWM/MOSI, 8_digit_7_segment_LED_Module_with_Max1.CLK
  N3: Part1.D12/MISO, 8_digit_7_segment_LED_Module_with_Max1.DIN
  GND: Part1.GND, 8_digit_7_segment_LED_Module_with_Max1.GND
  5V: Part1.5V, 8_digit_7_segment_LED_Module_with_Max1.VCC
