# Fritzing sketch 0300 - LED Direct Connect (saved by Fritzing 0.9.3b)
breadboards: 1

parts:
  LED1 = 7-SEGMENT-4-Digit-Panel-fineprint [package=7-segment-4digit-fineprint]
  LED2 = 7-SEGMENT-4-Digit-Panel-fineprint [package=7-segment-4digit-fineprint]
  R1 = Resistor [tolerance=±5% resistance=470 package=THT]
  R2 = Resistor [tolerance=±5% resistance=470 package=THT]
  R3 = Resistor [tolerance=±5% resistance=470 package=THT]
  R4 = Resistor [tolerance=±5% resistance=470 package=THT]
  R5 = Resistor [tolerance=±5% resistance=470 package=THT]
  R6 = Resistor [tolerance=±5% resistance=470 package=THT]
  R7 = Resistor [tolerance=±5% resistance=470 package=THT]
  Part1 = Arduino Uno (Rev3)

nets:
  N1: LED1.A, LED2.A, R1.Pin_1
  N2: LED1.B, LED2.B, R2.Pin_1
  N3: LED1.C, LED2.C, R3.Pin_1
  N4: LED1.D, LED2.D, R4.Pin_1
  N5: LED1.E, LED2.E, R5.Pin_1
  N6: LED1.F, LED2.F, R6.Pin_1
  N7: LED1.G, LED2.G, R7.Pin_1
  N8: LED2.DIG1, Part1.D13/SCK
  N9: LED2.DIG2, Part1.D12/MISO
  N10: LED2.DIG3, Part1.D11_PWM/MOSI
  N11: LED2.DIG4, Part1.D10_PWM/SS
  N12: R1.Pin_0, Part1.D2
  N13: R2.Pin_0, Part1.D3_PWM
  N14: R3.Pin_0, Part1.D4
  N15: R4.Pin_0, Part1.D5_PWM
  N16: R5.Pin_0, Part1.D6_PWM
  N17: R6.Pin_0, Part1.D7
  N18: R7.Pin_0, Part1.D8

notes:
  A -> G Segments

custom parts:
  7-SEGMENT-4-Digit-Panel-fineprint: This is a part for the 4-Digit 7-segment LEDs from FinePrint. This display panel only has 12 pins as it only has 4 digits consiting of 7 segments and a decimal place. There is no Colon nor apostrophe LED's.
