# Fritzing sketch BiColourLED (saved by Fritzing 0.9.4)
breadboards: 1

parts:
  Arduino_Uno = Arduino Uno (Rev3)
  R1 = Resistor [tolerance=±5% resistance=2k package=THT]
  R2 = Resistor [tolerance=±5% resistance=2k package=THT]
  R3 = Resistor [tolerance=±5% resistance=470 package=THT]
  LED1_-_bi-colour = LED - 5mm [color="Blue (470nm)" package="5 mm [THT]"]
  LED1 = DUO LED RG [package="5 mm [THT]"]
  R4 = Resistor [tolerance=±5% resistance=470 package=THT]

nets:
  N1: Arduino_Uno.A0, R1.Pin_1, R2.Pin_0
  N2: Arduino_Uno.D8, LED1_-_bi-colour.anode
  N3: Arduino_Uno.D9_PWM, LED1.green_anode
  N4: Arduino_Uno.D10_PWM/SS, LED1.red_anode
  N5: Arduino_Uno.GND, R1.Pin_0, R4.Pin_1
  N6: Arduino_Uno.D7, R3.Pin_0
  N7: Arduino_Uno.5V, R2.Pin_1
  N8: R3.Pin_1, LED1_-_bi-colour.cathode
  N9: LED1.common_cathode, R4.Pin_0
