# Fritzing sketch HABLoggerV01 (saved by Fritzing 0.9.3b)
breadboards: 1

parts:
  Part1 = OLED Monochrome 128x32 I2C [part_number=931]
  Teensy1 = Teensy 4.1
  Part3 = Logic Level Converter
  R1 = Resistor [tolerance=±5% resistance=1M package=THT]
  R2 = Resistor [tolerance=±5% resistance=1M package=THT]
  R3 = Resistor [tolerance=±5% resistance=680 package=THT]
  LED1 = LED - 5mm [color="Orange (605nm)" package="5 mm [THT]"]
  DS1 = DS18B20 1-Wire Temperature Sensor [part_number=DS18B20]
  DS2 = DS18B20 1-Wire Temperature Sensor [part_number=DS18B20]
  R4 = Resistor [tolerance=±5% resistance=4.7k package=THT]
  U1_(GPS) = SUP500F [package=sup500f]
  LED2 = LED - 5mm [color="Green (555nm)" package="5 mm [THT]"]
  R5 = Resistor [tolerance=±5% resistance=680 package=THT]

nets:
  3.3V: Part1.3.3V, Teensy1.Vin, Part3.HV, R2.Pin_0
  GND: Part1.GND, Teensy1.GND2#31, Part3.GND, R1.Pin_1, LED1.cathode, DS1.GND, DS2.GND, U1_(GPS).GND, LED2.cathode
  N1: Part1.SCL, Part3.RX_HV
  N2: Part1.SDA, Part3.TX_HV
  N3: Teensy1.GND, Teensy1.GND2#55
  N4: Teensy1.D0, U1_(GPS).RX-I
  N5: Teensy1.D1, U1_(GPS).TX-O
  N6: Teensy1.D10, DS1.DQ, DS2.DQ, R4.Pin_0
  N7: Teensy1.A0/D14, R1.Pin_0, R2.Pin_1
  N8: Teensy1.A4/D18, Part3.TX_LV
  N9: Teensy1.A5/D19, Part3.RX_LV
  VDD: Teensy1.3V3_LOW, Part3.LV, DS1.VDD, DS2.VDD, R4.Pin_1, U1_(GPS).VCC
  N10: Teensy1.D35, R5.Pin_0
  N11: Teensy1.D36, R3.Pin_0
  N12: R3.Pin_1, LED1.anode
  N13: LED2.anode, R5.Pin_1

notes:
  Green LED - record
  Orange LED - heater
  Green LED - record
  Yellow LED - heater
  Green LED: Record
  Orange LED: Heater

custom parts:
  OLED Monochrome 128x32 I2C: These displays are small, only about 1" diagonal, but very readable due to the high contrast of an OLED display. This display is made of 128x32 individual white OLED pixels, each one is turned on or off by the controller chip. Because the display makes its own light, no backlight is required. This reduces the power required to run the OLED and is why the display has such high contrast; we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
  Teensy 4.1: The Teensy is a complete USB-based microcontoller development system, in a very small footprint, capable of implementing many types of projects. All programming is done via the USB port. No special programmer is needed, only a standard micro-USB cable and a PC or Macintosh with a USB port.
