# Fritzing sketch Quarantine Clock (saved by Fritzing 0.9.4)
breadboards: 1

parts:
  Real_Time_Clock_Module = Real Time Clock Module - DS1307 RTC Breakout Board
  10_segment_Bar_LED = LED_BARGRAPH_10 [package=led_bargaph_10]
  Part2 = Arduino Mega 2560 (Rev3)
  R2 = Resistor [tolerance=±5% resistance=470 package=THT]
  R3 = Resistor [tolerance=±5% resistance=470 package=THT]
  R4 = Resistor [tolerance=±5% resistance=470 package=THT]
  R5 = Resistor [tolerance=±5% resistance=470 package=THT]
  R6 = Resistor [tolerance=±5% resistance=470 package=THT]
  R7 = Resistor [tolerance=±5% resistance=470 package=THT]
  R8 = Resistor [tolerance=±5% resistance=470 package=THT]
  R9 = Resistor [tolerance=±5% resistance=470 package=THT]
  R10 = Resistor [tolerance=±5% resistance=470 package=THT]
  R11 = Resistor [tolerance=±5% resistance=470 package=THT]
  R12 = Resistor [tolerance=±5% resistance=470 package=THT]
  R13 = Resistor [tolerance=±5% resistance=470 package=THT]
  R14 = Resistor [tolerance=±5% resistance=470 package=THT]
  R15 = Resistor [tolerance=±5% resistance=470 package=THT]
  R16 = Resistor [tolerance=±5% resistance=470 package=THT]
  R17 = Resistor [tolerance=±5% resistance=470 package=THT]
  R18 = Resistor [tolerance=±5% resistance=470 package=THT]
  R19 = Resistor [tolerance=±5% resistance=470 package=THT]
  LED1 = 7-SEGMENT-4-Digit-Clock-Panel-vishay [part_number=TDCG1060m package=7-segment-4digit-vishay]

nets:
  5V: Real_Time_Clock_Module.5V, Part2.5V
  GND: Real_Time_Clock_Module.GND, Part2.GND, R2.Pin_1, R3.Pin_1, R4.Pin_1, R5.Pin_1, R6.Pin_1, R7.Pin_1, R8.Pin_1, R9.Pin_1, R10.Pin_1, R11.Pin_1, LED1.L1-L2_Cathode
  N1: Real_Time_Clock_Module.SCL, Part2.D21/SCL
  N2: Real_Time_Clock_Module.SDA, Part2.D20/SDA
  N3: 10_segment_Bar_LED.A_A, R2.Pin_0
  N4: 10_segment_Bar_LED.B_A, R3.Pin_0
  N5: 10_segment_Bar_LED.C_A, R4.Pin_0
  N6: 10_segment_Bar_LED.D_A, R5.Pin_0
  N7: 10_segment_Bar_LED.E_A, R6.Pin_0
  N8: 10_segment_Bar_LED.F_A, R7.Pin_0
  N9: 10_segment_Bar_LED.G_A, R8.Pin_0
  N10: 10_segment_Bar_LED.H_A, R9.Pin_0
  N11: 10_segment_Bar_LED.I_A, R10.Pin_0
  N12: 10_segment_Bar_LED.J_A, R11.Pin_0
  N13: 10_segment_Bar_LED.J_C, Part2.D34
  N14: 10_segment_Bar_LED.I_C, Part2.D35
  N15: 10_segment_Bar_LED.H_C, Part2.D36
  N16: 10_segment_Bar_LED.G_C, Part2.D37
  N17: 10_segment_Bar_LED.F_C, Part2.D38
  N18: 10_segment_Bar_LED.E_C, Part2.D39
  N19: 10_segment_Bar_LED.D_C, Part2.D40
  N20: 10_segment_Bar_LED.C_C, Part2.D41
  N21: 10_segment_Bar_LED.B_C, Part2.D42
  N22: 10_segment_Bar_LED.A_C, Part2.D43
  N23: Part2.D3_PWM, LED1.D1
  N24: Part2.D4_PWM, LED1.D2
  N25: Part2.D5_PWM, LED1.D3
  N26: Part2.D6_PWM, LED1.D4
  N27: Part2.D22, R19.Pin_0
  N28: Part2.D23, R18.Pin_0
  N29: Part2.D24, R17.Pin_0
  N30: Part2.D25, R16.Pin_0
  N31: Part2.D26, R15.Pin_0
  N32: Part2.D27, R14.Pin_0
  N33: Part2.D28, R13.Pin_0
  N34: Part2.D29, R12.Pin_0
  N35: R12.Pin_1, LED1.L1-L2_Anode
  N36: R13.Pin_1, LED1.G
  N37: R14.Pin_1, LED1.F
  N38: R15.Pin_1, LED1.E
  N39: R16.Pin_1, LED1.D
  N40: R17.Pin_1, LED1.C
  N41: R18.Pin_1, LED1.B
  N42: R19.Pin_1, LED1.A

custom parts:
  7-SEGMENT-4-Digit-Clock-Panel-vishay: This is a part for the 4-Digit 7-segment LEDs from Vishay. This display panel has 16 pins that map to 4 x 8 segment LED digits (7 digit segments plus decimal point), a colon for use in a clock display and a "degree" symbol.
