# Fritzing sketch Quarantine Clock V02 (saved by Fritzing 0.9.4)
breadboards: 2

parts:
  Arduino_Mega_2560 = Arduino Mega 2560 (Rev3)
  LED1 = 7-SEGMENT-4-Digit-Clock-Panel-vishay [part_number=TDCG1060m package=7-segment-4digit-vishay]
  D1 = LED_BARGRAPH_10 [package=led_bargaph_10]
  R1 = Resistor [tolerance=±5% resistance=10k package=THT]
  R2 = Resistor [tolerance=±5% resistance=470 package=THT]
  R3 = Resistor [tolerance=±5% resistance=470 package=THT]
  R4 = Resistor [tolerance=±5% resistance=470 package=THT]
  R5 = Resistor [tolerance=±5% resistance=470 package=THT]
  R6 = Resistor [tolerance=±5% resistance=470 package=THT]
  R7 = Resistor [tolerance=±5% resistance=470 package=THT]
  R8 = Resistor [tolerance=±5% resistance=470 package=THT]
  R9 = Resistor [tolerance=±5% resistance=470 package=THT]
  R10 = Resistor [tolerance=±5% resistance=470 package=THT]
  R11 = Resistor [tolerance=±5% resistance=470 package=THT]
  R12 = Resistor [tolerance=±5% resistance=470 package=THT]
  R13 = Resistor [tolerance=±5% resistance=470 package=THT]
  R14 = Resistor [tolerance=±5% resistance=470 package=THT]
  R15 = Resistor [tolerance=±5% resistance=470 package=THT]
  R16 = Resistor [tolerance=±5% resistance=470 package=THT]
  R17 = Resistor [tolerance=±5% resistance=470 package=THT]
  R18 = Resistor [tolerance=±5% resistance=470 package=THT]
  R19 = Resistor [tolerance=±5% resistance=470 package=THT]
  R20 = Resistor [tolerance=±5% resistance=10k package=THT]
  R21 = Resistor [tolerance=±5% resistance=10k package=THT]
  R22 = Resistor [tolerance=±5% resistance=10k package=THT]
  R23 = Resistor [tolerance=±5% resistance=10k package=THT]
  R24 = Resistor [tolerance=±5% resistance=10k package=THT]
  R25 = Resistor [tolerance=±5% resistance=10k package=THT]
  R26 = Resistor [tolerance=±5% resistance=10k package=THT]
  Q2 = NPN-Transistor [part_number=BC337 package="TO92 [THT]"]
  Q3 = NPN-Transistor [part_number=BC337 package="TO92 [THT]"]
  Q4 = NPN-Transistor [part_number=BC337 package="TO92 [THT]"]
  Q5 = NPN-Transistor [part_number=BC337 package="TO92 [THT]"]
  Q6 = NPN-Transistor [part_number=BC337 package="TO92 [THT]"]
  Q7 = NPN-Transistor [part_number=BC337 package="TO92 [THT]"]
  Q8 = NPN-Transistor [part_number=BC337 package="TO92 [THT]"]
  R27 = Photocell (LDR) [package=THT]
  R28 = Resistor [tolerance=±5% resistance=2.2k package=THT]
  RTC = Real Time Clock Module - DS1307 RTC Breakout Board
  Q9 = NPN-Transistor [part_number=BC337 package="TO92 [THT]"]
  R29 = Resistor [tolerance=±5% resistance=47 package=THT]
  R30 = Resistor [tolerance=±5% resistance=47 package=THT]
  R32 = Resistor [tolerance=±5% resistance=47 package=THT]
  R33 = Resistor [tolerance=±5% resistance=47 package=THT]

nets:
  N1: Arduino_Mega_2560.A0, R27.pin_1, R28.Pin_1
  N2: Arduino_Mega_2560.D21/SCL, RTC.SCL
  N3: Arduino_Mega_2560.D20/SDA, RTC.SDA
  N4: Arduino_Mega_2560.D11_PWM, R24.Pin_0
  N5: Arduino_Mega_2560.D10_PWM, R25.Pin_0
  N6: Arduino_Mega_2560.D9_PWM, R26.Pin_0
  N7: Arduino_Mega_2560.D8_PWM, R23.Pin_0
  5V: Arduino_Mega_2560.5V, R27.pin_0, RTC.5V
  GND: Arduino_Mega_2560.GND, Q2.C, Q3.C, Q4.C, R28.Pin_0, RTC.GND, Q9.C, R29.Pin_1
  N8: Arduino_Mega_2560.D3_PWM, R22.Pin_0
  N9: Arduino_Mega_2560.D4_PWM, R21.Pin_0
  N10: Arduino_Mega_2560.D5_PWM, R20.Pin_0
  N11: Arduino_Mega_2560.D6_PWM, R1.Pin_0
  N12: Arduino_Mega_2560.D22, R3.Pin_0
  N13: Arduino_Mega_2560.D23, R2.Pin_0
  N14: Arduino_Mega_2560.D24, R5.Pin_0
  N15: Arduino_Mega_2560.D25, R6.Pin_0
  N16: Arduino_Mega_2560.D26, R7.Pin_0
  N17: Arduino_Mega_2560.D27, R8.Pin_0
  N18: Arduino_Mega_2560.D28, R9.Pin_0
  N19: Arduino_Mega_2560.D29, R10.Pin_0
  N20: Arduino_Mega_2560.D34, D1.J_C
  N21: Arduino_Mega_2560.D35, D1.I_C
  N22: Arduino_Mega_2560.D36, D1.H_C
  N23: Arduino_Mega_2560.D37, D1.G_C
  N24: Arduino_Mega_2560.D38, D1.F_C
  N25: Arduino_Mega_2560.D39, D1.E_C
  N26: Arduino_Mega_2560.D40, D1.D_C
  N27: Arduino_Mega_2560.D41, D1.C_C
  N28: Arduino_Mega_2560.D42, D1.B_C
  N29: Arduino_Mega_2560.D43, D1.A_C
  N30: LED1.D1, Q8.E
  N31: LED1.D2, Q7.E
  N32: LED1.D, R6.Pin_1
  N33: LED1.L1-L2_Cathode, R4.Pin_1, R11.Pin_1, R12.Pin_1, R13.Pin_1, R14.Pin_1, R15.Pin_1, R16.Pin_1, R17.Pin_1, R18.Pin_1, R19.Pin_1, Q2.E, Q5.C, Q6.C, Q7.C, Q8.C, R30.Pin_0
  N34: LED1.E, R7.Pin_1
  N35: LED1.D3, Q6.E
  N36: LED1.D4, Q5.E
  N37: LED1.F, R8.Pin_1
  N38: LED1.L1-L2_Anode, R10.Pin_1
  N39: LED1.C, R5.Pin_1
  N40: LED1.A, R3.Pin_1
  N41: LED1.G, R9.Pin_1
  N42: LED1.B, R2.Pin_1
  N43: D1.A_A, R19.Pin_0
  N44: D1.B_A, R18.Pin_0
  N45: D1.C_A, R17.Pin_0
  N46: D1.D_A, R16.Pin_0
  N47: D1.E_A, R15.Pin_0
  N48: D1.F_A, R14.Pin_0
  N49: D1.G_A, R13.Pin_0
  N50: D1.H_A, R12.Pin_0
  N51: D1.I_A, R11.Pin_0
  N52: D1.J_A, R4.Pin_0
  N53: R1.Pin_1, Q5.B
  N54: R20.Pin_1, Q6.B
  N55: R21.Pin_1, Q7.B
  N56: R22.Pin_1, Q8.B
  N57: R23.Pin_1, Q2.B
  N58: R24.Pin_1, Q4.B
  N59: R25.Pin_1, Q3.B
  N60: R26.Pin_1, Q9.B
  N61: Q3.E, R32.Pin_0, R33.Pin_1
  N62: Q4.E, R29.Pin_0, R32.Pin_1
  N63: Q9.E, R30.Pin_1, R33.Pin_0

notes:
  Brightness Control
  Digit Seln
  Digit Selection

custom parts:
  7-SEGMENT-4-Digit-Clock-Panel-vishay: This is a part for the 4-Digit 7-segment LEDs from Vishay. This display panel has 16 pins that map to 4 x 8 segment LED digits (7 digit segments plus decimal point), a colon for use in a clock display and a "degree" symbol.
