# Fritzing sketch StairLight Circuit (saved by Fritzing 0.9.3b)
circuit board: 8.46667cm x 5.64444cm
breadboards: 1

parts:
  J2_->_PIR = screw terminal, 3 pins
  R1_(LDR) = Photocell (LDR) [package=THT]
  R2 = Resistor [tolerance=±5% resistance=10k package=THT]
  R3 = Resistor [tolerance=±5% resistance=470 package=THT]
  J1_->_LED_Strip = Screw terminal - 2 pins [package=THT]
  Arduino_Leonardo = Arduino Leonardo (Rev3b)
  Q1 = Basic FET N-Channel [package="TO220 [THT]"]

nets:
  N1: J2_->_PIR.pin1, R2.Pin_0, Arduino_Leonardo.5V
  N2: J2_->_PIR.pin2, Arduino_Leonardo.D2/SDA
  N3: J2_->_PIR.pin3, R1_(LDR).pin_0, Arduino_Leonardo.GND, Q1.source
  N4: R1_(LDR).pin_1, R2.Pin_1, Arduino_Leonardo.A0
  N5: R3.Pin_0, Arduino_Leonardo.D3_PWM/SCL
  N6: R3.Pin_1, Q1.gate
  N7: J1_->_LED_Strip.pin1, Arduino_Leonardo.VIN
  N8: J1_->_LED_Strip.pin2, Q1.drain
