# Fritzing sketch TemperatureAndHumidityMonitor (saved by Fritzing 0.9.3b)
circuit board: 8.46667cm x 5.64444cm
breadboards: 1

parts:
  Part1 = Arduino Board Ethernet
  LED1 = LED - 5mm [color="Red (633nm)" package="5 mm [THT]"]
  R1 = Resistor [tolerance=±5% resistance=220 package=THT]
  DHT1 = DHT22 Temperature & Humidity Sensor Module [package="Arduino Module"]

nets:
  N1: Part1.D2_PWM, DHT1.S
  N2: Part1.D3_PWM, R1.Pin_1
  5V: Part1.5V, LED1.anode, DHT1.Vin
  N3: Part1.GND, DHT1.-
  N4: LED1.cathode, R1.Pin_0

custom parts:
  DHT22 Temperature & Humidity Sensor Module: DHT22 Arduino temperature and humidity sensor module.
